# Fritzing sketch CanINO (saved by Fritzing 0.9.10b)
breadboards: 1

parts:
  Part1 = Arduino Uno (Rev3)
  U1 = POT [knob_status=50% power=0.5W package=pot_mammoth]
  Grove1 = Grove OLED 128x96
  J2 = Basic Servo  # not connected
  J3 = Basic Servo  # not connected
  ZS-042_RTC1 = ZS-042 RTC Module  # not connected
  Part2 = HX711 Weighing Sensor Module  # not connected
  S1 = Pushbutton [package="[SMD]"]
  U5 = SWITCH-SPST-2 [package=switch-spst-vertical]

nets:
  N1: Part1.A0, U1.A
  N2: Part1.A4/SDA, Grove1.SCL
  N3: Part1.A5/SCL, Grove1.SDA
  N4: Part1.D2, U5.P
  N5: Part1.D3_PWM, S1.Pin_3, S1.Pin_4
  5V: Part1.5V, U1.S, Grove1.VCC, S1.Pin_1, S1.Pin_2
  GND: Part1.GND, U1.E, Grove1.GND, U5.O
